# Fritzing sketch Car Circuit (saved by Fritzing 0.9.3b)

parts:
  Composant1 = Arduino Nano (Rev3.0)
  Composant2 = Bluetooth HC-05 Macho
  J1 = Basic Servo
  JP1 = Header 3 [package=screwterminal-3.5mm-3_lock.007s]

nets:
  GND: Composant1.GND, Composant2.GND, J1.gnd, JP1.3
  N1: Composant1.D5, JP1.1
  N2: Composant1.D9, Composant2.Key
  N3: Composant1.D10, Composant2.TXD
  N4: Composant1.D11/MOSI, Composant2.RXD
  VCC: Composant2.VCC, J1.vcc
