# Fritzing sketch Controller Circuit (saved by Fritzing 0.9.3b)

parts:
  Composant2 = Bluetooth HC-05 Macho
  Composant1 = Arduino Nano (Rev3.0)
  Composant3 = Thumb Joystick
  VCC1 = Battery block 9V
  Composant4 = Thumb Joystick

nets:
  N1: Composant2.TXD, Composant1.D10
  N2: Composant2.RXD, Composant1.D11/MOSI
  VCC: Composant2.VCC, Composant1.5V, Composant3.VCC, Composant4.VCC
  N3: Composant2.Key, Composant1.D9
  GND: Composant2.GND, Composant1.GND, Composant3.GND, VCC1.-, Composant4.GND
  N4: Composant1.VIN, VCC1.+
  N5: Composant1.A4, Composant3.VERT
  N6: Composant1.A0, Composant4.HORZ
